# Fritzing sketch arduino_operation_game (saved by Fritzing 0.9.4)
breadboards: 1

parts:
  Part1 = Arduino Nano (Rev3.0)
  SP1 = SPEAKER [package=pcb_mount_speaker]
  LED1 = LED - 5mm [color="Red (633nm)" package="5 mm [THT]"]
  R1 = Resistor [tolerance=±5% resistance=330 package=THT]

nets:
  N1: Part1.GND, SP1.+, LED1.cathode
  N2: Part1.D11/MOSI, SP1.-
  N3: Part1.D13/SCK, R1.Pin_1
  N4: LED1.anode, R1.Pin_0

notes:
  --> to metal tweezers
  to game metal plate -->
